// Logisim project 7400.circ as structural Verilog: 1 circuit, main circuit main
module main (
);

  wire n7400_1_pin1, n7400_1_pin2, n7400_1_pin3;

  _7400 u_7400_1 (
    .pin1(n7400_1_pin1), .pin2(n7400_1_pin2), .pin3(n7400_1_pin3));  // open: pin4, pin5, pin6, pin13, pin12, pin11, pin10, pin9, pin8
  // DipSwitch #(.NSwitches(1)) _1A: pin names not known; wires that end beside it: n7400_1_pin1
  // DipSwitch #(.NSwitches(1)) _1B: pin names not known; wires that end beside it: n7400_1_pin2
  LED _1Y (.in(n7400_1_pin3));
endmodule
