// Logisim project DeMorganII.circ as structural Verilog: 1 circuit, main circuit main
module main (
);

  wire and_1_out, nor_1_out, y_p1, y_p2;

  // DipSwitch #(.NSwitches(1)) x: pin names not known
  // DipSwitch #(.NSwitches(1)) y: pin names not known; wires that end beside it: y_p1, y_p2
  and and_1 (and_1_out, ~y_p1, ~y_p2);  // AND_Gate
  LED led_1 (.in(nor_1_out));
  nor nor_1 (nor_1_out, y_p1, y_p2);
  LED led_2 (.in(and_1_out));
endmodule
