// Logisim project DeMorganIII.circ as structural Verilog: 1 circuit, main circuit main
module main (
);

  wire nand_1_out, or_1_out, y_p1, y_p2;

  // DipSwitch #(.NSwitches(1)) x: pin names not known
  // DipSwitch #(.NSwitches(1)) y: pin names not known; wires that end beside it: y_p1, y_p2
  or or_1 (or_1_out, ~y_p1, ~y_p2);  // OR_Gate
  LED led_1 (.in(nand_1_out));
  nand nand_1 (nand_1_out, y_p1, y_p2);
  LED led_2 (.in(or_1_out));
endmodule
