// Logisim project PortaAND.circ as structural Verilog: 1 circuit, main circuit main
module main (
);

  wire and_1_out, b_p1, b_p2;

  // DipSwitch #(.NSwitches(1)) a: pin names not known
  LED S (.in(and_1_out));
  // DipSwitch #(.NSwitches(1)) b: pin names not known; wires that end beside it: b_p1, b_p2
  and and_1 (and_1_out, b_p1, b_p2);
endmodule
