// Logisim project PortaNOR.circ as structural Verilog: 1 circuit, main circuit main
module main (
);

  wire b_p1, b_p2, nor_1_out;

  // DipSwitch #(.NSwitches(1)) a: pin names not known
  // DipSwitch #(.NSwitches(1)) b: pin names not known; wires that end beside it: b_p1, b_p2
  nor nor_1 (nor_1_out, b_p1, b_p2);
  LED S (.in(nor_1_out));
endmodule
