// Logisim project PortaNOT.circ as structural Verilog: 1 circuit, main circuit main
module main (
);

  wire a_p1, not_1_out;

  // DipSwitch #(.NSwitches(1)) a: pin names not known; wires that end beside it: a_p1
  LED S (.in(not_1_out));
  not not_1 (not_1_out, a_p1);
endmodule
