// Logisim project ContFF_T_DecrescenteMod16.circ as structural Verilog: 1 circuit, main circuit main
module main (
);

  wire CLK_out, CLR_p1, t_ff_1_q, t_ff_2_q, t_ff_3_q;
  wire [3:0] t_ff_1_qn;

  Clock CLK (.out(CLK_out));
  // DipSwitch #(.NSwitches(1)) CLR: pin names not known; wires that end beside it: CLR_p1
  T_Flip_Flop #(.trigger("falling"), .NegatePresetClear("true")) t_ff_1 (
    .clk(CLK_out), .T(1'b1), .Q(t_ff_1_q), .Qn(t_ff_1_qn[0]), .reset(CLR_p1));  // open: preset
  Hex_Digit_Display hex_digit_display_1 (.value(t_ff_1_qn));  // open: dp
  T_Flip_Flop #(.trigger("falling"), .NegatePresetClear("true")) t_ff_2 (
    .clk(t_ff_1_q), .T(1'b1), .Q(t_ff_2_q), .Qn(t_ff_1_qn[1]), .reset(CLR_p1));  // open: preset
  T_Flip_Flop #(.trigger("falling"), .NegatePresetClear("true")) t_ff_3 (
    .clk(t_ff_2_q), .T(1'b1), .Q(t_ff_3_q), .Qn(t_ff_1_qn[2]), .reset(CLR_p1));  // open: preset
  T_Flip_Flop #(.trigger("falling"), .NegatePresetClear("true")) t_ff_4 (
    .clk(t_ff_3_q), .T(1'b1), .Qn(t_ff_1_qn[3]), .reset(CLR_p1));  // open: Q, preset

  // Notes on the sheet:
  //   /Q0
  //   /Q1
  //   /Q2
  //   /Q3
endmodule
