// Logisim project ContFF_T_OSC.circ as structural Verilog: 1 circuit, main circuit main
module main (
);

  wire CLK_out, CLR_p1, digital_oscilloscope_1_p2, digital_oscilloscope_1_p3, digital_oscilloscope_1_p4,
       digital_oscilloscope_1_p5, digital_oscilloscope_1_p6;

  Clock CLK (.out(CLK_out));
  // DipSwitch #(.NSwitches(1)) CLR: pin names not known; wires that end beside it: CLR_p1
  // Digital_Oscilloscope #(.nState(16)) digital_oscilloscope_1: pin names not known; wires that end beside it: CLK_out, digital_oscilloscope_1_p2, digital_oscilloscope_1_p3, digital_oscilloscope_1_p4, digital_oscilloscope_1_p5, digital_oscilloscope_1_p6
  T_Flip_Flop #(.trigger("falling"), .NegatePresetClear("true")) t_ff_1 (
    .clk(CLK_out), .T(1'b1), .Q(digital_oscilloscope_1_p2), .reset(CLR_p1));  // open: Qn, preset
  Button CLR_2 (.out(digital_oscilloscope_1_p6));
  T_Flip_Flop #(.trigger("falling"), .NegatePresetClear("true")) t_ff_2 (
    .clk(digital_oscilloscope_1_p2), .T(1'b1), .Q(digital_oscilloscope_1_p3), .reset(CLR_p1));  // open: Qn, preset
  T_Flip_Flop #(.trigger("falling"), .NegatePresetClear("true")) t_ff_3 (
    .clk(digital_oscilloscope_1_p3), .T(1'b1), .Q(digital_oscilloscope_1_p4), .reset(CLR_p1));  // open: Qn, preset
  LED Q3 (.in(digital_oscilloscope_1_p5));
  T_Flip_Flop #(.trigger("falling"), .NegatePresetClear("true")) t_ff_4 (
    .clk(digital_oscilloscope_1_p4), .T(1'b1), .Q(digital_oscilloscope_1_p5), .reset(CLR_p1));  // open: Qn, preset
  LED Q1 (.in(digital_oscilloscope_1_p3));
  LED Q2 (.in(digital_oscilloscope_1_p4));
  LED Q0 (.in(digital_oscilloscope_1_p2));

  // Notes on the sheet:
  //   CLK
  //   Q0
  //   Q1
  //   Q2
  //   Q3
endmodule
