// Logisim project FF_T.circ as structural Verilog: 1 circuit, main circuit main
module main (
);

  wire CLK_out, t_ff_1_q, T_p1;

  Clock CLK (.out(CLK_out));
  // DipSwitch #(.NSwitches(1)) T: pin names not known; wires that end beside it: T_p1
  T_Flip_Flop t_ff_1 (.clk(CLK_out), .T(T_p1), .Q(t_ff_1_q));  // open: Qn, preset, reset
  LED led_1 (.in(t_ff_1_q));
endmodule
