// Logisim project ex1.circ as structural Verilog: 1 circuit, main circuit main
module main (
);

  wire CLK_out, CLR_p1, digital_oscilloscope_1_p5, digital_oscilloscope_1_p6, t_ff_1_q, t_ff_2_q, t_ff_3_q;

  Clock CLK (.out(CLK_out));
  // DipSwitch #(.NSwitches(1)) CLR: pin names not known; wires that end beside it: CLR_p1
  T_Flip_Flop #(.trigger("falling"), .NegatePresetClear("true")) t_ff_1 (
    .clk(CLK_out), .T(1'b1), .Q(t_ff_1_q), .reset(CLR_p1));  // open: Qn, preset
  T_Flip_Flop #(.trigger("falling"), .NegatePresetClear("true")) t_ff_2 (
    .clk(t_ff_1_q), .T(1'b1), .Q(t_ff_2_q), .reset(CLR_p1));  // open: Qn, preset
  T_Flip_Flop #(.trigger("falling"), .NegatePresetClear("true")) t_ff_3 (
    .clk(t_ff_2_q), .T(1'b1), .Q(t_ff_3_q), .reset(CLR_p1));  // open: Qn, preset
  // Digital_Oscilloscope #(.nState(16)) digital_oscilloscope_1: pin names not known; wires that end beside it: CLK_out, t_ff_1_q, t_ff_2_q, t_ff_3_q, digital_oscilloscope_1_p5, digital_oscilloscope_1_p6
  T_Flip_Flop #(.trigger("falling"), .NegatePresetClear("true")) t_ff_4 (
    .clk(t_ff_3_q), .T(1'b1), .Q(digital_oscilloscope_1_p5), .reset(CLR_p1));  // open: Qn, preset
  Button CLR_2 (.out(digital_oscilloscope_1_p6));

  // Notes on the sheet:
  //   CLK
  //   Q0
  //   Q1
  //   Q2
  //   Q3
endmodule
