// Logisim project ex1b.circ as structural Verilog: 1 circuit, main circuit main
module main (
);

  wire CLK_out, CLR_p1, digital_oscilloscope_1_p5, t_ff_1_q, t_ff_1_qn, t_ff_2_q, t_ff_2_qn, t_ff_3_qn;

  Clock CLK (.out(CLK_out));
  // DipSwitch #(.NSwitches(1)) CLR: pin names not known; wires that end beside it: CLR_p1
  T_Flip_Flop #(.trigger("falling"), .NegatePresetClear("true")) t_ff_1 (
    .clk(CLK_out), .T(1'b1), .Q(t_ff_1_q), .Qn(t_ff_1_qn), .reset(CLR_p1));  // open: preset
  T_Flip_Flop #(.trigger("falling"), .NegatePresetClear("true")) t_ff_2 (
    .clk(t_ff_1_q), .T(1'b1), .Q(t_ff_2_q), .Qn(t_ff_2_qn), .reset(CLR_p1));  // open: preset
  T_Flip_Flop #(.trigger("falling"), .NegatePresetClear("true")) t_ff_3 (
    .clk(t_ff_2_q), .T(1'b1), .Qn(t_ff_3_qn), .reset(CLR_p1));  // open: Q, preset
  // Digital_Oscilloscope #(.nState(7)) digital_oscilloscope_1: pin names not known; wires that end beside it: CLK_out, t_ff_1_qn, t_ff_2_qn, t_ff_3_qn, digital_oscilloscope_1_p5
  Button CLR_2 (.out(digital_oscilloscope_1_p5));

  // Notes on the sheet:
  //   CLK
  //   Q0
  //   Q1
  //   Q2
endmodule
