// Logisim project ex2a.circ as structural Verilog: 1 circuit, main circuit main
module main (
);

  wire and_1_out, and_2_out, CLK_out, digital_oscilloscope_1_p5, digital_oscilloscope_1_p6, t_ff_1_q,
       t_ff_2_q, t_ff_3_q;

  Clock CLK (.out(CLK_out));
  T_Flip_Flop #(.NegatePresetClear("true")) t_ff_1 (.clk(CLK_out), .T(1'b1), .Q(t_ff_1_q));  // open: Qn, preset, reset
  T_Flip_Flop #(.NegatePresetClear("true")) t_ff_2 (
    .clk(CLK_out), .T(t_ff_1_q), .Q(t_ff_2_q));  // open: Qn, preset, reset
  and and_1 (and_1_out, t_ff_2_q, t_ff_1_q);
  T_Flip_Flop #(.NegatePresetClear("true")) t_ff_3 (
    .clk(CLK_out), .T(and_1_out), .Q(t_ff_3_q));  // open: Qn, preset, reset
  and and_2 (and_2_out, t_ff_3_q, t_ff_2_q, t_ff_1_q);
  // Digital_Oscilloscope #(.nState(16)) digital_oscilloscope_1: pin names not known; wires that end beside it: CLK_out, t_ff_1_q, t_ff_2_q, t_ff_3_q, digital_oscilloscope_1_p5, digital_oscilloscope_1_p6
  T_Flip_Flop #(.NegatePresetClear("true")) t_ff_4 (
    .clk(CLK_out), .T(and_2_out), .Q(digital_oscilloscope_1_p5));  // open: Qn, preset, reset
  Button CLN (.out(digital_oscilloscope_1_p6));

  // Notes on the sheet:
  //   Q2
  //   Q3
  //   CLK
  //   Q0
  //   Q1
endmodule
