// Logisim project ex6.circ as structural Verilog: 1 circuit, main circuit main
module main (
);

  wire and_1_out, and_2_out, CLR_p1, digital_oscilloscope_1_p1, not_1_out, xor_1_out;
  wire [0:0] digital_oscilloscope_1_p9;
  wire [2:0] digital_oscilloscope_1_p2;
  wire [3:0] digital_oscilloscope_1_p5;

  // Digital_Oscilloscope #(.nState(15)) digital_oscilloscope_1: pin names not known; wires that end beside it: digital_oscilloscope_1_p1, digital_oscilloscope_1_p2[0], digital_oscilloscope_1_p2[1], digital_oscilloscope_1_p2[2], digital_oscilloscope_1_p5[0], digital_oscilloscope_1_p5[1], digital_oscilloscope_1_p5[2], digital_oscilloscope_1_p5[3], digital_oscilloscope_1_p9[0]
  not not_1 (not_1_out, and_2_out);
  Clock CLK (.out(digital_oscilloscope_1_p1));
  D_Flip_Flop d_ff_1 (
    .clk(digital_oscilloscope_1_p1), .D(digital_oscilloscope_1_p2[1]), .Q(digital_oscilloscope_1_p5[0]));  // open: Qn, preset, reset
  and and_1 (and_1_out, not_1_out, digital_oscilloscope_1_p1);
  // DipSwitch #(.NSwitches(1)) CLR: pin names not known; wires that end beside it: CLR_p1, digital_oscilloscope_1_p5[2]
  D_Flip_Flop d_ff_2 (
    .clk(digital_oscilloscope_1_p1), .D(digital_oscilloscope_1_p5[0]), .Q(digital_oscilloscope_1_p5[1]));  // open: Qn, preset, reset
  T_Flip_Flop #(.trigger("falling"), .NegatePresetClear("true")) t_ff_1 (
    .clk(and_1_out), .T(1'b1), .Q(digital_oscilloscope_1_p2[0]), .reset(CLR_p1));  // open: Qn, preset
  D_Flip_Flop d_ff_3 (
    .clk(digital_oscilloscope_1_p1), .D(digital_oscilloscope_1_p5[1]), .Q(digital_oscilloscope_1_p5[2]));  // open: Qn, preset, reset
  and and_2 (and_2_out, digital_oscilloscope_1_p5[2], xor_1_out);
  T_Flip_Flop #(.trigger("falling"), .NegatePresetClear("true")) t_ff_2 (
    .clk(digital_oscilloscope_1_p2[0]), .T(1'b1), .Q(digital_oscilloscope_1_p2[1]), .reset(CLR_p1));  // open: Qn, preset
  D_Flip_Flop d_ff_4 (
    .clk(digital_oscilloscope_1_p1), .D(digital_oscilloscope_1_p5[2]), .Q(digital_oscilloscope_1_p5[3]));  // open: Qn, preset, reset
  xor xor_1 (xor_1_out, digital_oscilloscope_1_p5[2], digital_oscilloscope_1_p5[3]);
  T_Flip_Flop #(.trigger("falling"), .NegatePresetClear("true")) t_ff_3 (
    .clk(digital_oscilloscope_1_p2[1]), .T(1'b1), .Q(digital_oscilloscope_1_p2[2]), .reset(CLR_p1));  // open: Qn, preset
  D_Flip_Flop d_ff_5 (
    .clk(digital_oscilloscope_1_p1), .D(digital_oscilloscope_1_p5[3]), .Q(digital_oscilloscope_1_p9[0]));  // open: Qn, preset, reset
  Hex_Digit_Display hex_digit_display_1 (.value({1'b0, digital_oscilloscope_1_p2}));  // open: dp
  Hex_Digit_Display hex_digit_display_2 (.value({3'b000, digital_oscilloscope_1_p9[0]}));  // open: dp
  Hex_Digit_Display hex_digit_display_3 (.value(digital_oscilloscope_1_p5));  // open: dp

  // Notes on the sheet:
  //   Q2
  //   Q3
  //   Q4
  //   CLK
  //   Q0
  //   Q1
  //   Q2
  //   Q0
  //   Q1
  //   Q0
  //   Q0
  //   Q1
  //   Q1
  //   Q2
  //   Q2
  //   Q3
  //   Q4
endmodule
