// Logisim project FF_JK_OSC.circ as structural Verilog: 1 circuit, main circuit main
module main (
  output out_1
);

  wire digital_oscilloscope_1_p1, digital_oscilloscope_1_p2, digital_oscilloscope_1_p3, K_p2;

  // Digital_Oscilloscope digital_oscilloscope_1: pin names not known; wires that end beside it: digital_oscilloscope_1_p1, digital_oscilloscope_1_p2, digital_oscilloscope_1_p3, out_1
  // DipSwitch #(.NSwitches(1)) J: pin names not known; wires that end beside it: digital_oscilloscope_1_p2
  Clock CLK (.out(digital_oscilloscope_1_p1));
  // DipSwitch #(.NSwitches(1)) K: pin names not known; wires that end beside it: digital_oscilloscope_1_p3, K_p2
  J_K_Flip_Flop j_k_ff_1 (
    .J(digital_oscilloscope_1_p2), .clk(digital_oscilloscope_1_p1), .K(digital_oscilloscope_1_p3), .Q(out_1));  // open: Qn, preset, reset
  Button button_1 (.out(K_p2));

  // Notes on the sheet:
  //   CLK
  //   J
  //   K
  //   Q
endmodule
