// Logisim project FF_RS_OSC.circ as structural Verilog: 1 circuit, main circuit main
module main (
  output out_1
);

  wire digital_oscilloscope_1_p1, R_p1, S_p1;

  // Digital_Oscilloscope digital_oscilloscope_1: pin names not known; wires that end beside it: digital_oscilloscope_1_p1, out_1
  Clock clock_1 (.out(digital_oscilloscope_1_p1));
  // DipSwitch #(.NSwitches(1)) S: pin names not known; wires that end beside it: S_p1
  // DipSwitch #(.NSwitches(1)) R: pin names not known; wires that end beside it: R_p1
  S_R_Flip_Flop s_r_ff_1 (.S(S_p1), .clk(digital_oscilloscope_1_p1), .R(R_p1), .Q(out_1));  // open: Qn, preset, reset
endmodule
