// Logisim project FF_T_OSC.circ as structural Verilog: 1 circuit, main circuit main
module main (
  output out_1
);

  wire digital_oscilloscope_1_p1, digital_oscilloscope_1_p2, digital_oscilloscope_1_p4;

  // Digital_Oscilloscope digital_oscilloscope_1: pin names not known; wires that end beside it: digital_oscilloscope_1_p1, digital_oscilloscope_1_p2, out_1, digital_oscilloscope_1_p4
  Clock CLK (.out(digital_oscilloscope_1_p1));
  // DipSwitch #(.NSwitches(1)) T: pin names not known; wires that end beside it: digital_oscilloscope_1_p2
  T_Flip_Flop t_ff_1 (
    .clk(digital_oscilloscope_1_p1), .T(digital_oscilloscope_1_p2), .Q(out_1));  // open: Qn, preset, reset
  Button button_1 (.out(digital_oscilloscope_1_p4));

  // Notes on the sheet:
  //   CLK
  //   T
  //   Q
endmodule
