// Logisim project LatchRSPositivo.circ as structural Verilog: 1 circuit, main circuit main
module main (
  input  SET,
  input  RESET
);

  wire nor_1_out, nor_2_out;

  LED nQ (.in(nor_1_out));
  nor nor_1 (nor_1_out, SET, nor_2_out);
  LED Q (.in(nor_2_out));
  nor nor_2 (nor_2_out, nor_1_out, RESET);
endmodule
