// Logisim project Bin2Oct.circ as structural Verilog: 1 circuit, main circuit main
module main (
  input  C,
  input  B,
  input  A
);

  wire _0_out, _1_out, _2_out, _3_out, _4_out, _5_out, _6_out, _7_out, not_1_out, not_2_out, not_3_out;

  not not_1 (not_1_out, C);
  not not_2 (not_2_out, B);
  not not_3 (not_3_out, A);
  LED nC__B__A (.in(_0_out));
  and _0 (_0_out, not_3_out, not_2_out, not_1_out);
  and _1 (_1_out, not_1_out, not_2_out, A);
  LED nC__B_A (.in(_1_out));
  and _2 (_2_out, not_1_out, B, not_3_out);
  LED nC_B__A (.in(_2_out));
  and _3 (_3_out, not_1_out, B, A);
  LED nC_B_A (.in(_3_out));
  and _4 (_4_out, C, not_2_out, not_3_out);
  LED C__B__A (.in(_4_out));
  LED C__B_A (.in(_5_out));
  and _5 (_5_out, C, not_2_out, A);
  LED C_B__A (.in(_6_out));
  and _6 (_6_out, C, B, not_3_out);
  and _7 (_7_out, A, B, C);
  LED C_B_A (.in(_7_out));
endmodule
