// Logisim project FuncDemux.circ as structural Verilog: 1 circuit, main circuit main
module main (
  input  A,
  input  B,
  input  C
);

  wire demultiplexer_1_out0, demultiplexer_1_out1, demultiplexer_1_out6, demultiplexer_1_out7, or_1_out,
       or_2_out;

  Demultiplexer #(.select(3), .enable("false")) demultiplexer_1 (
    .out0(demultiplexer_1_out0), .out1(demultiplexer_1_out1), .out6(demultiplexer_1_out6),
    .out7(demultiplexer_1_out7), .in(1'b1), .sel({A, B, C}));  // open: out2, out3, out4, out5
  or or_1 (or_1_out, demultiplexer_1_out0, demultiplexer_1_out1);
  LED F1 (.in(or_1_out));
  LED F2 (.in(or_2_out));
  or or_2 (or_2_out, demultiplexer_1_out6, demultiplexer_1_out7);
endmodule
