// Logisim project FF_D.circ as structural Verilog: 1 circuit, main circuit main
module main (
);

  wire CLK_out, d_ff_1_q, D_p1;

  Clock CLK (.out(CLK_out));
  // DipSwitch #(.NSwitches(1)) D: pin names not known; wires that end beside it: D_p1
  D_Flip_Flop d_ff_1 (.clk(CLK_out), .D(D_p1), .Q(d_ff_1_q));  // open: Qn, preset, reset
  LED led_1 (.in(d_ff_1_q));
endmodule
