// Logisim project Reg_FF_D_CargaParalela.circ as structural Verilog: 1 circuit, main circuit main
module main (
  input  in_1,
  input  in_2,
  input  in_3
);

  wire CLK_p1, d_ff_1_q, d_ff_2_q, d_ff_3_q;

  // DipSwitch #(.NSwitches(1)) CLK: pin names not known; wires that end beside it: CLK_p1
  LED Q0 (.in(d_ff_1_q));
  D_Flip_Flop #(.trigger("falling")) d_ff_1 (.clk(CLK_p1), .D(in_1), .Q(d_ff_1_q));  // open: Qn, preset, reset
  LED Q1 (.in(d_ff_2_q));
  D_Flip_Flop #(.trigger("falling")) d_ff_2 (.clk(CLK_p1), .D(in_2), .Q(d_ff_2_q));  // open: Qn, preset, reset
  LED Q2 (.in(d_ff_3_q));
  D_Flip_Flop #(.trigger("falling")) d_ff_3 (.clk(CLK_p1), .D(in_3), .Q(d_ff_3_q));  // open: Qn, preset, reset
endmodule
