// Logisim project Reg_FF_D_CargaParalela_LOAD_OSC.circ as structural Verilog: 1 circuit, main circuit main
module main (
  input  in_1,
  input  in_2,
  input  in_3
);

  wire digital_oscilloscope_1_p1, digital_oscilloscope_1_p2, digital_oscilloscope_1_p3,
       digital_oscilloscope_1_p4, digital_oscilloscope_1_p5, LOAD_p1, multiplexer_1_out, multiplexer_2_out,
       multiplexer_3_out;

  // Digital_Oscilloscope #(.nState(16)) digital_oscilloscope_1: pin names not known; wires that end beside it: digital_oscilloscope_1_p1, digital_oscilloscope_1_p2, digital_oscilloscope_1_p3, digital_oscilloscope_1_p4, digital_oscilloscope_1_p5
  Clock CLK (.out(digital_oscilloscope_1_p1));
  Multiplexer #(.enable("false")) multiplexer_1 (
    .in0(digital_oscilloscope_1_p2), .in1(in_1), .out(multiplexer_1_out), .sel(LOAD_p1));
  // DipSwitch #(.NSwitches(1)) LOAD: pin names not known; wires that end beside it: LOAD_p1
  Button button_1 (.out(digital_oscilloscope_1_p5));
  LED Q0 (.in(digital_oscilloscope_1_p2));
  D_Flip_Flop #(.trigger("falling")) d_ff_1 (
    .clk(digital_oscilloscope_1_p1), .D(multiplexer_1_out), .Q(digital_oscilloscope_1_p2));  // open: Qn, preset, reset
  Multiplexer #(.enable("false")) multiplexer_2 (
    .in0(digital_oscilloscope_1_p3), .in1(in_2), .out(multiplexer_2_out), .sel(LOAD_p1));
  LED Q1 (.in(digital_oscilloscope_1_p3));
  D_Flip_Flop #(.trigger("falling")) d_ff_2 (
    .clk(digital_oscilloscope_1_p1), .D(multiplexer_2_out), .Q(digital_oscilloscope_1_p3));  // open: Qn, preset, reset
  Multiplexer #(.enable("false")) multiplexer_3 (
    .in0(digital_oscilloscope_1_p4), .in1(in_3), .out(multiplexer_3_out), .sel(LOAD_p1));
  LED Q2 (.in(digital_oscilloscope_1_p4));
  D_Flip_Flop #(.trigger("falling")) d_ff_3 (
    .clk(digital_oscilloscope_1_p1), .D(multiplexer_3_out), .Q(digital_oscilloscope_1_p4));  // open: Qn, preset, reset

  // Notes on the sheet:
  //   CLK
  //   Q0
  //   Q1
  //   Q2
endmodule
