// Logisim project Reg_FF_D_Transf.circ as structural Verilog: 1 circuit, main circuit main
module main (
);

  wire CLK_p1, d_ff_1_q, d_ff_2_q, d_ff_3_q, Din_p1;

  // DipSwitch #(.NSwitches(1)) CLK: pin names not known; wires that end beside it: CLK_p1
  // DipSwitch #(.NSwitches(1)) Din: pin names not known; wires that end beside it: Din_p1
  LED Q0 (.in(d_ff_1_q));
  D_Flip_Flop #(.trigger("falling")) d_ff_1 (.clk(CLK_p1), .D(Din_p1), .Q(d_ff_1_q));  // open: Qn, preset, reset
  LED D0 (.in(Din_p1));
  LED Q1 (.in(d_ff_2_q));
  D_Flip_Flop #(.trigger("falling")) d_ff_2 (.clk(CLK_p1), .D(d_ff_1_q), .Q(d_ff_2_q));  // open: Qn, preset, reset
  LED D1 (.in(d_ff_1_q));
  LED Q2 (.in(d_ff_3_q));
  D_Flip_Flop #(.trigger("falling")) d_ff_3 (.clk(CLK_p1), .D(d_ff_2_q), .Q(d_ff_3_q));  // open: Qn, preset, reset
  LED D2 (.in(d_ff_2_q));
endmodule
